# Fritzing sketch variable_pitch_oscillator (saved by Fritzing 0.9.3b)
breadboards: 1

parts:
  L2 = Inductor [package="400 mil [THT]"]
  C2 = Electrolytic Capacitor [capacitance=10pF package="100 mil [THT, electrolytic]"]
  Q1 = NPN-Transistor [package="TO92 [THT]"]
  R1 = Resistor [tolerance=±5% resistance=2.2k package="2512 [SMD]"]
  Q2 = NPN-Transistor [package="TO92 [THT]"]
  R2 = Resistor [tolerance=±5% resistance=1k package=THT]
  R3 = Resistor [tolerance=±5% resistance=47k package=THT]
  R4 = Resistor [tolerance=±5% resistance=1k package=THT]
  C4 = Electrolytic Capacitor [capacitance=1µF package="100 mil [THT, electrolytic]"]

nets:
  N1: L2.pin_0, C2.-, C4.-
  12V: L2.pin_1, C2.+, Q1.C
  N2: Q1.E, R1.Pin_1
  N3: Q1.B, R4.Pin_1
  -12V: R1.Pin_0
  N4: Q2.B, R2.Pin_0, R3.Pin_0
  GND: R2.Pin_1, R4.Pin_0, C4.+
